# Fritzing sketch WR (saved by Fritzing 0.9.10b)
circuit board: 8.46667cm x 5.64444cm
breadboards: 1

parts:
  U1 = ESP32S-HiLetgo [part_number=ESP32S-HiLetgo]
  OLED_I2C1_4Wire = OLED 128x64 I2C Monochrome Display
  C5 = Electrolytic Capacitor [capacitance=1mF voltage=16V package="100 mil [THT, electrolytic]"]
  Power_plug1 = Power plug
  DS18B20 = TMP36 Temperature Sensor [package="TO92 [THT]"]
  Pulsante = Round Pushbutton
  R1 = Resistor [tolerance=±5% resistance=1200 package="0402 [SMD]"]
  RGB_Cat_com = RGB LED (com. cathode, rgb) [package="5 mm [THT]"]
  R2 = Resistor [tolerance=±5% resistance=4700 package="0402 [SMD]"]

nets:
  N1: U1.GPIO14, RGB_Cat_com.red_anode
  N2: U1.GPIO12, RGB_Cat_com.green_anode
  N3: U1.GPIO13, RGB_Cat_com.blue_anode
  N4: U1.GPIO2, Pulsante.leg1, R1.Pin_0
  N5: U1.GPIO4, R2.Pin_0
  N6: U1.GPIO21, OLED_I2C1_4Wire.SDA
  N7: U1.GPIO22, OLED_I2C1_4Wire.SCK
  N8: OLED_I2C1_4Wire.VDD, DS18B20.+Vs, Pulsante.leg0
  GND: OLED_I2C1_4Wire.GND, DS18B20.GND, R1.Pin_1
  N9: C5.-, Power_plug1.GND, RGB_Cat_com.common_cathode
  N10: C5.+, Power_plug1.VCC
  N11: DS18B20.Vout, R2.Pin_1

notes:
  Lettore temperatura per esperienza con bomba di Mahler

custom parts:
  ESP32S-HiLetgo: HiLetgo ESP-WROOM-32 ESP32 ESP-32S Development Board 2.4GHz Dual-Mode WiFi + Bluetooth Dual Cores Microcontroller The ESP32 integrated with Antenna switches, RF Balun, power amplifiers, low-noise amplifiers, filters, and management modules, and the entire solution occupies the least area of PCB. 2.4 GHz Wi-Fi plus Bluetooth dual-mode chip, with TSMC Ultra-low power consumption 40nm technology,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
